// Logisim project lab11_3.circ as structural Verilog: 1 circuit, main circuit main
module main (
  input  in_1,
  input  A0,
  input  A1,
  input  A2,
  input  A3,
  input  A4,
  input  A5,
  input  A6,
  input  A7,
  input  in_10,
  input  in_11,
  output Q4,
  output Q5,
  output Q6,
  output Q7,
  output Q0,
  output Q1,
  output Q2,
  output Q3
);

  wire clock_1_out, n74162_synch_decade_counter_1_tc;

  Clock clock_1 (.out(clock_1_out));
  _74162__synch_decade_counter u_74162_synch_decade_counter_1 (
    .SR(in_11), .CET(1'b1), .CEP(1'b1), .PE(in_1), .P0(A0), .P1(A1), .P2(A2), .P3(A3), .CP(clock_1_out),
    .TC(n74162_synch_decade_counter_1_tc), .Q0(Q0), .Q1(Q1), .Q2(Q2), .Q3(Q3));
  _74163__synch_binary_counter u_74163_synch_binary_counter_1 (
    .A(A4), .B(A5), .C(A6), .D(A7), .LOAD(in_1), .ENP(1'b1), .ENT(n74162_synch_decade_counter_1_tc), .QA(Q4),
    .QB(Q5), .QC(Q6), .QD(Q7), .RCO(in_10), .CLK(clock_1_out), .CLEAR(in_11));
endmodule
