// Logisim project lab11_6.circ as structural Verilog: 1 circuit, main circuit main
module main (
  input  in_1,
  input  in_2,
  input  in_3,
  input  in_4,
  input  in_5,
  input  in_6,
  input  in_7,
  input  in_8,
  input  in_9,
  output out_10,
  output out_11,
  output out_12,
  output out_13,
  output out_14,
  output out_15,
  output out_16,
  output out_17
);

  wire clock_1_out, n74193_up_down_binary_counter_1_borrow, n74193_up_down_binary_counter_1_carry, nand_1_out;

  Clock clock_1 (.out(clock_1_out));
  _74193__up_down_binary_counter u_74193_up_down_binary_counter_1 (
    .CDn(1'b1), .CUp(clock_1_out), .BORROW(n74193_up_down_binary_counter_1_borrow),
    .CARRY(n74193_up_down_binary_counter_1_carry), .QA(out_14), .QB(out_15), .QC(out_16), .QD(out_17),
    .LOAD(nand_1_out), .CLEAR(in_9), .D(in_4), .C(in_3), .B(in_2), .A(in_1));
  _74193__up_down_binary_counter u_74193_up_down_binary_counter_2 (
    .CDn(n74193_up_down_binary_counter_1_borrow), .CUp(n74193_up_down_binary_counter_1_carry), .QA(out_10),
    .QB(out_11), .QC(out_12), .QD(out_13), .LOAD(nand_1_out), .CLEAR(in_9), .D(in_8), .C(in_7), .B(in_6),
    .A(in_5));  // open: BORROW, CARRY
  nand nand_1 (nand_1_out, out_12, out_17, out_15);
endmodule
