// Logisim project ex7.circ as structural Verilog: 1 circuit, main circuit main
module main (
  input  Q,
  input  J,
  input  K,
  input  in_4,
  output out_5,
  output out_6
);

  wire and_1_out, and_2_out, or_1_out;

  and and_1 (and_1_out, ~Q, J);  // AND_Gate
  and and_2 (and_2_out, ~K, Q);  // AND_Gate
  or or_1 (or_1_out, and_1_out, and_2_out);
  _7474__D_flip_flop_w__clear___preset u_7474_d_flip_flop_w_clear_preset_1 (
    .CLK(in_4), .D(or_1_out), .Q(out_5), .Q_2(out_6), .PR(1'b1), .CLR(1'b1));
endmodule
