// Logisim project lab5 ex6 p0.circ as structural Verilog: 1 circuit, main circuit main
module main (
  input  A,
  input  C,
  input  D,
  output p0
);

  wire and_1_out;

  and and_1 (and_1_out, A, C);
  or or_1 (p0, and_1_out, D);
endmodule
