// Logisim project lab5 ex6 p2.circ as structural Verilog: 1 circuit, main circuit main
module main (
  input  A,
  input  b,
  input  c,
  input  D,
  output out_5
);

  wire and_1_out, and_2_out, and_3_out;

  and and_1 (and_1_out, ~A, ~D, b);  // AND_Gate
  and and_2 (and_2_out, ~b, ~c, D);  // AND_Gate
  and and_3 (and_3_out, ~A, b, c);  // AND_Gate
  or or_1 (out_5, and_1_out, A, and_2_out, and_3_out);
endmodule
