// Logisim project ex5.circ as structural Verilog: 1 circuit, main circuit main
module main (
  input  A,
  input  s1,
  input  s0,
  output out_4,
  output out_5,
  output out_6,
  output out_7
);

  wire demultiplexer_1_out0, demultiplexer_1_out1;

  Demultiplexer #(.enable("false")) demultiplexer_1 (
    .out0(demultiplexer_1_out0), .out1(demultiplexer_1_out1), .in(A), .sel(s1));
  Demultiplexer #(.enable("false")) demultiplexer_2 (.out0(out_4), .out1(out_5), .in(demultiplexer_1_out0), .sel(s0));
  Demultiplexer #(.enable("false")) demultiplexer_3 (.out0(out_6), .out1(out_7), .in(demultiplexer_1_out1), .sel(s0));
endmodule
