// Logisim project ex8.circ as structural Verilog: 1 circuit, main circuit main
module main (
  input  A3,
  input  A2,
  input  A1,
  input  A0,
  output F3,
  output F2,
  output F1,
  output F0
);

  xor xor_1 (F2, A3, A2);
  xor xor_2 (F1, A2, A1);
  xor xor_3 (F0, A2, A0);

  assign F3 = A3;
endmodule
