// Logisim project lab10_5.circ as structural Verilog: 1 circuit, main circuit main
module main (
  input  RST,
  output Q1,
  output Q0,
  output Q2
);

  wire clock_1_out;

  Clock clock_1 (.out(clock_1_out));
  _7473__JK_flip_flop_w__clear u_7473_jk_flip_flop_w_clear_1 (
    .Q(Q0), .CLR(RST), .J(1'b1), .CLK(clock_1_out), .K(1'b1));  // open: Q_2
  _7473__JK_flip_flop_w__clear u_7473_jk_flip_flop_w_clear_2 (
    .Q(Q1), .CLR(RST), .J(1'b1), .CLK(Q0), .K(1'b1));  // open: Q_2
  _7473__JK_flip_flop_w__clear u_7473_jk_flip_flop_w_clear_3 (
    .Q(Q2), .CLR(RST), .J(1'b1), .CLK(Q1), .K(1'b1));  // open: Q_2
endmodule
