// Logisim project lab11_4.circ as structural Verilog: 1 circuit, main circuit main
module main (
  input  in_1,
  input  in_2,
  input  in_3,
  input  in_4,
  input  in_5,
  input  in_6,
  output out_7,
  output out_8,
  output out_9,
  output out_10
);

  wire n74192_up_down_decade_counter_1_tcd;

  _74192__up_down_decade_counter u_74192_up_down_decade_counter_1 (
    .CPD(in_5), .CPU(1'b1), .P0(in_1), .P1(in_2), .P2(in_3), .P3(in_4),
    .PL(n74192_up_down_decade_counter_1_tcd), .MR(in_6), .TCD(n74192_up_down_decade_counter_1_tcd),
    .Q0(out_7), .Q1(out_8), .Q2(out_9), .Q3(out_10));  // open: TCU
endmodule
