// Logisim project lab11_5.circ as structural Verilog: 1 circuit, main circuit main
module main (
  input  in_1,
  input  in_2,
  input  in_3,
  input  in_4,
  output out_5,
  output out_6,
  output out_7,
  output out_8,
  output out_9
);

  wire clock_1_out, nand_1_out;

  Clock clock_1 (.out(clock_1_out));
  _74162__synch_decade_counter u_74162_synch_decade_counter_1 (
    .SR(in_4), .CET(1'b1), .CEP(1'b1), .PE(nand_1_out), .P0(in_1), .P1(in_2), .P2(1'b1), .P3(in_3),
    .CP(clock_1_out), .TC(out_5), .Q0(out_6), .Q1(out_7), .Q2(out_8), .Q3(out_9));
  nand nand_1 (nand_1_out, out_9, out_6);
endmodule
